# Fritzing sketch Sonar (saved by Fritzing 0.9.4)

parts:
  WeMos_D1_Mini1 = WeMos D1 Mini
  Part1 = TP4056 Charger
  BAT1 = Battery Holders [package=battery-aa]
  HC-SR04_Sensor_1 = HC-SR04 Ultrasonic Distance Sensor

nets:
  5V: WeMos_D1_Mini1.5V, Part1.BAT+, BAT1.+, HC-SR04_Sensor_1.VCC
  N1: WeMos_D1_Mini1.D1, HC-SR04_Sensor_1.TRIG
  N2: WeMos_D1_Mini1.D2, HC-SR04_Sensor_1.ECHO
  N3: WeMos_D1_Mini1.G, Part1.BAT-, BAT1.-, HC-SR04_Sensor_1.GND

custom parts:
  Battery Holders: Battery Holders Various common sizes : AA, AAA, 20mm coin cell and 12mm coin cell.
