# Fritzing sketch LCDTaunt (saved by Fritzing 0.9.2b)
circuit board: 12.2369cm x 8.3186cm
breadboards: 1

parts:
  TTP223B1 = TTP223B Capacitive Touch Sensor Module
  LCD1 = LCD screen
  R1 = Rotary Potentiometer (Small) [maximum_resistance=10kΩ package=THT]
  R2 = Resistor [tolerance=±5% resistance=10k package=THT]
  Part1 = Arduino Uno (Rev3)

nets:
  GND: TTP223B1.GND, LCD1.VSS, LCD1.R/W, LCD1.LED-, R1.leg1, Part1.GND
  VCC: TTP223B1.VCC, LCD1.VDD, R1.leg2, R2.Pin_0, Part1.5V
  N1: TTP223B1.SIG, Part1.D7
  N2: LCD1.V0, R1.wiper
  N3: LCD1.RS, Part1.D12/MISO
  N4: LCD1.E, Part1.D11_PWM/MOSI
  N5: LCD1.DB4, Part1.D5_PWM
  N6: LCD1.DB5, Part1.D4
  N7: LCD1.DB6, Part1.D3_PWM
  N8: LCD1.DB7, Part1.D2
  N9: LCD1.LED+, R2.Pin_1

custom parts:
  TTP223B Capacitive Touch Sensor Module: The TTP223B capacitive touch sensor module uses the TTP223B IC. The appropriate voltage is approximately 2 to 5.5 volts.

// code stored in the sketch: LCDTaunt.ino
// Periodically taunts user to touch sensor, if touched shouts at user, rudely thanks them for letting off, and back to taunt cycle

// This is a fun little project to turn your Arduino into a bit of a bully. It will periodically display a taunting message to the user
// and when the touch sensor is touched, it will display a threatening message, and then when the touch is removed, it will display a
// quippy thanks message. Of course, it doesn't have to be a bully, as you can change the messages displayed in the arrays to be any
// messages you like, add more, or limit them to one message each, it's up to you. The componenets you will need are:
// 1. 16 x 2 LCD display
// 2. 10k rotary potentiometer
// 3. TTP223B touch sensor, or similar
// 4. 10k resistor

// LCD Circuit
// LCD Pin 1 :  VSS  -> GND
// LCD Pin 2 :  VDD  -> 5V
// LCD Pin 3 :  V0   -> Middle pin of 10k pot
// LCD Pin 4 :  RS   -> Arduino D12
// LCD Pin 5 :  RW   -> GND
// LCD Pin 6 :  E    -> Arduino D11
// LCD Pin 7 :  D0   -> N/A
// LCD Pin 8 :  D1   -> N/A
// LCD Pin 9 :  D2   -> N/A
// LCD Pin 10 : D3   -> N/A
// LCD Pin 11 : D4   -> Arduino D5
// LCD Pin 12 : D5   -> Arduino D4
// LCD Pin 13 : D6   -> Arduino D3
// LCD Pin 14 : D7   -> Arduino D2
// LCD Pin 15 : A    -> 10k res     -> 5V
// LCD Pin 16 : K    -> GND

// Potentiometer Circuit
// Outter 10k pot pin to 5V
// Middle pin to LCD Pin 3 (V0)
// Outter 10k pot pin to GND

// Sensor VCC pin -> 5V
// Sensor GND pin -> GND
// Sensor SIG pin -> Arduino D7

// include the library code for LCD
#include <LiquidCrystal.h>

// initialize the LCD library with the numbers of the interface pins
LiquidCrystal lcd(12, 11, 5, 4, 3, 2);

// Pin for touch sensor signal
int touchPin = 7;
// variable to keep track of latest change in touch state
int sensorState;

// thanks variables
// are we currently displaying a thanks message
bool thanking;
// duration in milliseconds that we want the thanks message displayed
long thanksDuration = 2000;
// time in milliseconds when thanks message is first displayed
long thanksMillis;
// array holding our thanks messages, a thanks message will be randomly selected each thanks cycle
const String thanks[] = {"THANKS YA JERK!", "THATS RIGHT!", "THOUGHT SO!"};

// taunt variables
// are we currently displaying a taunt message
bool taunting;
// delay in milliseconds before next taunt, either from startup or from last thanks or taunt cycle
long tauntDelay = 5000;
// duration in milliseconds that we want the taunt message displayed
long tauntDuration = 2000;
// time in milliseconds when taunt is first displayed
long tauntMillis;
// array holding our taunt messages, a taunt message will be randomly selected each taunt cycle
const String taunts[] = {"COME AT ME BRO!", "HEY UGLY!", "YO MOMMA!", "QUIT STARING!"};

// threat variables
// are we currently displaying a threat message
bool threatening;
// duration in milliseconds that we want our threat message displayed before thanking cycle starts
long threatDuration = 500;
// time in millis when threat message is first displayed
long threatMillis;
// array holding our threat messages, a threat message will be randomly selected each threat cycle
const String threats[] = {"DONT TOUCH ME!", "BACK OFF JACK!", "STEP OFF YO!", "HEY STOP!"};

void setup() 
{
  // set sensorState to be LOW so taunt cycle starts
  sensorState = LOW;
  // start taunt cycle countdown
  tauntMillis = millis();
  // initialize booleans to false
  thanking = false;
  taunting = false;
  threatening = false;
  // configure touch sensor signal pint to be INPUT
  pinMode(touchPin, INPUT);
  // initialize lcd, specifying the rows and column count, in our case 16 columns by 2 rows
  lcd.begin(16, 2);
}

void loop() 
{
  // read current touch state of touch sensor, it will be HIGH if touched, LOW if not touched
  int state = digitalRead(touchPin);
  
  // if state is touched
  if(state == HIGH)
  {
    // if our last known state was not touched, and we now have a touched state then we need to
    // start a threat cycle
    if(sensorState == LOW)
    {
      // set the value of our latest touch state to touched
      sensorState = HIGH;
      // since we are about to threaten, we are not taunting or thanking, set them to false
      thanking = false;
      taunting = false;
      // display a random threat message
      threaten();
      threatening = true;
    }
  }
  // current state is LOW
  else
  {
    // if our last known state was touched, and we now have a not touched state, we need to
    // start countdown for threat message
    if(sensorState == HIGH)
    {
      // set the value of our latest touch state to not touched
      sensorState = LOW;
      // start countdown to threat message removal
      threatMillis = millis();
    }
    // if threat cycle is active
    else if(threatening)
    {
      // check to see if threat duration has elapsed
      if(millis() - threatMillis > threatDuration)
      {
        // clear lcd output
        lcd.clear();
        // now we are no longer threatening
        threatening = false;
        // start thanks cycle
        thank();
        thanking = true;
        // start countdown to thanks message removal
        thanksMillis = millis();
      }
    }
    // if thanks cycle is active
    else if(thanking)
    {
      // check to see if thanks duration has elapsed
      if(millis() - thanksMillis > thanksDuration)
      {
        // clear lcd output
        lcd.clear();
        thanking = false;
        // start countdown till next taunt cycle
        tauntMillis = millis();
      }
    }
    // if taunt cycle is active
    else if(taunting)
    {
      // check to see if taunt duration has elapsed
      if(millis() - tauntMillis > tauntDuration)
      {
        // clear the lcd output
        lcd.clear();
        taunting = false;
        // start countdown to next taunt cycle
        tauntMillis = millis();
      }
    }
    // check to see if delay till next taunt cycle has elapsed
    else if(millis() - tauntMillis > tauntDelay)
    {
      // start a new taunt cycle
      taunt();
      taunting = true;
      // start countdown till taunt message removal
      tauntMillis = millis();
    }
  }  
}

// display random taunt message to lcd
void taunt()
{
    // determine length of taunt message array
    int tauntsLength = sizeof(taunts) / sizeof(*taunts);
    // get random number between 0 and taunt message array length
    int tauntIndex = rand() % tauntsLength;
    // clear lcd output
    lcd.clear();
    // set lcd cursor to top leftmost position
    lcd.setCursor(0, 0);
    // display message from random index in taunt message array
    lcd.print(taunts[tauntIndex]);
}

// display a random thanks message to lcd
void thank()
{
    // determine length of thanks message array
    int thanksLength = sizeof(thanks) / sizeof(*thanks);
    // get random number between 0 and thanks message array length
    int thanksIndex = rand() % thanksLength;
    // clear lcd output
    lcd.clear();
    // set lcd cursor to top leftmost position
    lcd.setCursor(0, 0);
    // display message from random index in thanks message array
    lcd.print(thanks[thanksIndex]);
}

// display random threat message to lcd
void threaten()
{
    // determind length of threat message array
    int threatsLength = sizeof(threats) / sizeof(*threats);
    // get random number between 0 and threat message array length
    int threatIndex = rand() % threatsLength;
    // clear lcd output
    lcd.clear();
    // set lcd cursor to top leftmost position
    lcd.setCursor(0, 0);
    // display message from random index of threat message array
    lcd.print(threats[threatIndex]);
}
